# Fritzing sketch pressure-sensor (saved by Fritzing 0.9.3b)

parts:
  Part1 = Arduino Pro
  Part2 = Arduino Pro Mini v13
  Part3 = FTDI Basic Programmer  # not connected
  IC1 = DIP - 8 pins [chip_label=pressure package="DIP (Dual Inline) [THT]"]
  IC2 = DIP - 8 pins [chip_label=pressure package="DIP (Dual Inline) [THT]"]

nets:
  N1: Part1.A4, IC2.pin8
  N2: Part1.A5, IC2.pin7
  N3: Part1.D10_PWM/SS, Part2.D10_PWM/SS
  N4: Part1.D11/MOSI, Part2.D11_PWM/MOSI
  N5: Part1.D12/MISO, Part2.D12/MISO
  N6: Part1.D13/SCK, Part2.D13/SCK
  N7: Part2.A4, IC1.pin8
  N8: Part2.A5, IC1.pin7

custom parts:
  DIP - 8 pins: A DIP stand-in part for whatever IC you want. With 8 pins on a 300mil dual inline package (DIP) footprint.
